# Fritzing sketch AllComponentsCleaned(mainProject) (saved by Fritzing 0.9.5d)
circuit board: 8.46667cm x 5.64444cm
breadboards: 2

parts:
  ESP32_-_Back1 = ESP32 - CAM
  Mic1 = KY-038
  Part1 = Arduino Uno (Rev3)
  LED1 = smd LED [color="Red (633nm)" package="1206 [SMD]"]
  M2 = Dagu DGServo 9g (Top view) [part_number=RS001B]
  M3 = Dagu DGServo 9g (Top view) [part_number=RS001B]
  LED4 = smd LED [color="Green (555nm)" package="1206 [SMD]"]
  BAT1 = Battery Holders [package=battery-aa-panel]  # not connected
  VCC1 = Battery
  VCC2 = Battery
  VCC3 = Battery
  VCC4 = Battery
  U1 = 74HC595 [package="DIP16 [THT]"]
  R1 = Resistor [tolerance=±5% resistance=220 package="0402 [SMD]"]
  R4 = Resistor [tolerance=±5% resistance=220 package="0402 [SMD]"]
  R5 = Resistor [tolerance=±5% resistance=220 package="0402 [SMD]"]
  R6 = Resistor [tolerance=±5% resistance=220 package="0402 [SMD]"]
  R7 = Resistor [tolerance=±5% resistance=220 package="0402 [SMD]"]
  R8 = Resistor [tolerance=±5% resistance=220 package="0402 [SMD]"]
  R9 = Resistor [tolerance=±5% resistance=220 package="0402 [SMD]"]
  LED6 = smd LED [color="Blue (430nm)" package="0805 [SMD]"]
  LED7 = smd LED [color="Blue (430nm)" package="0805 [SMD]"]
  LED8 = smd LED [color="Blue (430nm)" package="0805 [SMD]"]
  LED9 = smd LED [color="Blue (430nm)" package="0805 [SMD]"]
  LED10 = smd LED [color="Blue (430nm)" package="0805 [SMD]"]
  LED11 = smd LED [color="Blue (430nm)" package="0805 [SMD]"]
  LED12 = smd LED [color="Blue (430nm)" package="0805 [SMD]"]
  R10 = Resistor [tolerance=±5% resistance=220 package="0402 [SMD]"]
  LED13 = smd LED [color="Blue (430nm)" package="0805 [SMD]"]
  R11 = Resistor [tolerance=±5% resistance=1k package="0805 [SMD]"]
  R16 = Resistor [tolerance=±5% resistance=1k package="0805 [SMD]"]
  R18 = Resistor [tolerance=±5% resistance=1k package="0805 [SMD]"]

nets:
  N1: ESP32_-_Back1.GPIO13, Part1.D4, R11.Pin_0
  GND: ESP32_-_Back1.GND, Mic1.pin2, Part1.GND, LED1.cathode, M2.gnd, M3.gnd, LED4.cathode
  5V: ESP32_-_Back1.5V, Mic1.pin3, Part1.5V, R18.Pin_0
  N2: ESP32_-_Back1.GPIO3_/_RX, R11.Pin_1, R16.Pin_0
  N3: Mic1.pin1, Part1.A0
  N4: Mic1.pin4, Part1.D2
  N5: Part1.D9_PWM, M3.pulse
  N6: Part1.D10_PWM/SS, M2.pulse
  N7: Part1.D11_PWM/MOSI, U1.SH_CP
  N8: Part1.D12/MISO, U1.ST_CP
  N9: Part1.D13/SCK, LED4.anode
  N10: Part1.D3_PWM, U1.DS
  N11: Part1.D7, LED1.anode
  VCC: M2.vcc, M3.vcc, VCC3.+
  N12: VCC1.-, U1.OE, LED6.cathode, LED7.cathode, LED8.cathode, LED9.cathode, LED10.cathode, LED11.cathode, LED12.cathode, LED13.cathode
  N13: VCC1.+, VCC2.-
  N14: VCC2.+, U1.MR, U1.VCC
  N15: VCC3.-, VCC4.+
  N16: U1.Q1, R4.Pin_1
  N17: U1.Q2, R5.Pin_1
  N18: U1.Q3, R6.Pin_1
  N19: U1.Q4, R7.Pin_1
  N20: U1.Q5, R8.Pin_1
  N21: U1.Q6, R9.Pin_1
  N22: U1.Q7, R10.Pin_1
  N23: U1.Q0, R1.Pin_1
  N24: R1.Pin_0, LED6.anode
  N25: R4.Pin_0, LED7.anode
  N26: R5.Pin_0, LED8.anode
  N27: R6.Pin_0, LED9.anode
  N28: R7.Pin_0, LED10.anode
  N29: R8.Pin_0, LED11.anode
  N30: R9.Pin_0, LED12.anode
  N31: R10.Pin_0, LED13.anode
  N32: R16.Pin_1, R18.Pin_1

notes:
  the above one is motar 1 digital pin is 10 and it is motorpin1
  the below one is motorpin2 here digital pin is 9
  here in our arudino we have two pins for 5v pin so other than that all the connection are accurate
  220 ohms resistor , 8 blue leds
  In the actual practical project, I have used 1.2-volt rechargeable batteries that are 2100 mAh
  The 4-battery pack has a nominal voltage of 4.8 V, and when fully charged, the voltage rises to about 5.6 V.

custom parts:
  ESP32 - CAM: The ESP32-CAM has a very competitive small-size camera module that can operate independently as a minimum system with a footprint of only 27*40.5*4.5mm and a deep sleep current of up to 6mA.
  KY-038: ky-038 Microphone sound sensor module
